# Fritzing sketch SGK (saved by Fritzing 0.9.3b)
circuit board: 8.46667cm x 5.64444cm
breadboards: 1

parts:
  S1 = Pushbutton [package="[SMD]"]
  Raspberry_Pi_1 = Raspberry Pi 3 [part_number=RPI-3-V1.2]
  U1 = 2-Channel 5v Relay Shield [package=relay-2ch5v10a]
  Power_plug1 = Power plug
  M1 = DC Motor

nets:
  N1: S1.Pin_1, S1.Pin_2, Raspberry_Pi_1.GPIO18
  GND: S1.Pin_3, S1.Pin_4, Raspberry_Pi_1.GND, U1.GND
  N2: Raspberry_Pi_1.GPIO23, U1.IN1
  5V: Raspberry_Pi_1.5V, U1.VCC
  N3: U1.K1-In, M1.pin_2
  N4: U1.K1-Off, Power_plug1.GND
  N5: U1.K1-On, U1.K2-Off, U1.K2-On
  N6: Power_plug1.VCC, M1.pin_1

custom parts:
  2-Channel 5v Relay Shield: 2 Channel 5v Relay Shield w. 2x SPD-06VDC-SD-C
